// Logisim project 4-Bit Register.circ as structural Verilog: 1 circuit, main circuit main
module main (
  input  write_enable,
  input  [1:0] RegRead1,
  input  [1:0] write_select,
  input  [3:0] data_Input,
  input  [1:0] RegRead2,
  output [3:0] ReadPoint1,
  output [3:0] ReadPoint2
);

  wire and_1_out, and_2_out, and_3_out, and_4_out, clock_out, decoder_1_out0, decoder_1_out1, decoder_1_out2,
       decoder_1_out3;
  wire [3:0] R0_q, R1_q, R3_q, R4_q;

  Clock clock (.out(clock_out));
  Decoder #(.select(2), .enable("false")) decoder_1 (
    .out0(decoder_1_out0), .out1(decoder_1_out1), .out2(decoder_1_out2), .out3(decoder_1_out3),
    .sel(write_select));
  and and_1 (and_1_out, write_enable, decoder_1_out0);
  and and_2 (and_2_out, write_enable, decoder_1_out1);
  and and_3 (and_3_out, write_enable, decoder_1_out2);
  and and_4 (and_4_out, write_enable, decoder_1_out3);
  Register #(.width(4)) R0 (.D(data_Input), .en(and_1_out), .Q(R0_q), .clk(clock_out));  // open: clr
  Register #(.width(4)) R1 (.D(data_Input), .en(and_2_out), .Q(R1_q), .clk(clock_out));  // open: clr
  Register #(.width(4)) R3 (.D(data_Input), .en(and_3_out), .Q(R3_q), .clk(clock_out));  // open: clr
  Register #(.width(4)) R4 (.D(data_Input), .en(and_4_out), .Q(R4_q), .clk(clock_out));  // open: clr
  Multiplexer #(.select(2), .width(4), .enable("false")) multiplexer_1 (
    .in0(R0_q), .in1(R1_q), .in2(R3_q), .in3(R4_q), .out(ReadPoint1), .sel(RegRead1));
  Multiplexer #(.select(2), .width(4), .enable("false")) multiplexer_2 (
    .in0(R0_q), .in1(R1_q), .in2(R3_q), .in3(R4_q), .out(ReadPoint2), .sel(RegRead2));
endmodule
