// Logisim project 4-bit AU New.circ as structural Verilog: 1 circuit, main circuit main
module main (
  input  A,
  input  [3:0] A_2,
  input  [3:0] B,
  input  [1:0] in_4,
  output [3:0] Y,
  output Cout
);

  wire main_1_cout, main_2_cout, main_3_cout;

  _1_bit_AU_main main_1 (.Cin(A), .A(A_2[0]), .B(B[0]), .S1S0(in_4), .D(Y[0]), .Cout(main_1_cout));
  _1_bit_AU_main main_2 (.Cin(main_1_cout), .A(A_2[1]), .B(B[1]), .S1S0(in_4), .D(Y[1]), .Cout(main_2_cout));
  _1_bit_AU_main main_3 (.Cin(main_2_cout), .A(A_2[2]), .B(B[2]), .S1S0(in_4), .D(Y[2]), .Cout(main_3_cout));
  _1_bit_AU_main main_4 (.Cin(main_3_cout), .A(A_2[3]), .B(B[3]), .S1S0(in_4), .D(Y[3]), .Cout(Cout));
endmodule
