// Logisim project 4-bit AU.circ as structural Verilog: 1 circuit, main circuit main
module main (
  input  Cin,
  input  [3:0] A,
  input  [3:0] B,
  input  [1:0] S1S0,
  output [3:0] D,
  output Cout
);

  wire [3:0] multiplexer_1_out, not_1_out, not_2_out;

  assign not_1_out = ~B;  // NOT_Gate not_1, 4 bits wide
  assign not_2_out = ~4'b0000;  // NOT_Gate not_2, 4 bits wide
  Multiplexer #(.select(2), .width(4)) multiplexer_1 (
    .in0(B), .in1(not_1_out), .in2(4'b0000), .in3(not_2_out), .out(multiplexer_1_out), .sel(S1S0));  // open: en
  Adder #(.width(4)) adder_1 (.a(A), .b(multiplexer_1_out), .out(D), .cin(Cin), .cout(Cout));
endmodule
