// Logisim project Full Adder using  4X1 MUX.circ as structural Verilog: 1 circuit, main circuit main
module main (
  input  C,
  input  B,
  input  A,
  input  X,
  input  Y,
  output S,
  output CARRY
);

  wire not_1_out;

  not not_1 (not_1_out, C);
  MUX_main main_1 (.S1(B), .S0(A), .A3(C), .A2(not_1_out), .A1(not_1_out), .A0(C), .out_7(S));
  MUX_main main_2 (.S1(B), .S0(A), .A3(X), .A2(C), .A1(C), .A0(Y), .out_7(CARRY));

  // Notes on the sheet:
  //   C
  //   B
  //   A
endmodule
