// Logisim project Full Subtractor using 4X1 MUX.circ as structural Verilog: 1 circuit, main circuit main
module main (
  input  A,
  input  B,
  input  Bin,
  input  in_4,
  input  in_5,
  output out_6,
  output out_7
);

  wire not_1_out;

  not not_1 (not_1_out, Bin);
  MUX_main main_1 (.S1(A), .S0(B), .A3(Bin), .A2(not_1_out), .A1(not_1_out), .A0(Bin), .out_7(out_6));
  MUX_main main_2 (.S1(A), .S0(B), .A3(Bin), .A2(in_4), .A1(in_5), .A0(Bin), .out_7(out_7));
endmodule
