// Logisim project Half Subtractor using 4X1 MUX.circ as structural Verilog: 1 circuit, main circuit main
module main (
  input  in_1,
  input  in_2,
  input  A,
  input  B,
  input  in_5,
  input  in_6,
  output DIFFERENCE,
  output BORROW
);

  MUX_main main_1 (.S1(A), .S0(B), .A3(in_1), .A2(in_2), .A1(in_2), .A0(in_1), .out_7(DIFFERENCE));
  MUX_main main_2 (.S1(A), .S0(B), .A3(in_5), .A2(in_5), .A1(in_6), .A0(in_5), .out_7(BORROW));

  // Notes on the sheet:
  //   A
  //   B
  //   Diff
  //   Borrow
endmodule
