// Logisim project Parallel Adder.circ as structural Verilog: 1 circuit, main circuit main
module main (
  input  C,
  input  [3:0] A,
  input  [3:0] B,
  output [3:0] S,
  output Cout
);

  wire main_1_y, main_2_y, main_3_y;

  lab3_fullAdder_main main_1 (.a(C), .b(A[0]), .c(B[0]), .x(S[0]), .y(main_1_y));
  lab3_fullAdder_main main_2 (.a(main_1_y), .b(A[1]), .c(B[1]), .x(S[1]), .y(main_2_y));
  lab3_fullAdder_main main_3 (.a(main_2_y), .b(A[2]), .c(B[2]), .x(S[2]), .y(main_3_y));
  lab3_fullAdder_main main_4 (.a(main_3_y), .b(A[3]), .c(B[3]), .x(S[3]), .y(Cout));
endmodule
